// Logisim project Basic8Bit.circ as structural Verilog
module ALU (
  input  [7:0] A,
  input  [7:0] B,
  input  [1:0] ALU_Op,
  output [7:0] ALU_Out
);

  wire and_1_out;
  wire [7:0] adder_1_out, and_2_out, multiplexer_1_out, not_1_out, or_1_out;

  Multiplexer #(.width(8), .enable("false")) multiplexer_1 (
    .in0(B), .in1(not_1_out), .out(multiplexer_1_out), .sel(and_1_out));
  assign not_1_out = ~B;  // NOT_Gate not_1, 8 bits wide
  and and_1 (and_1_out, ALU_Op[0], ALU_Op[1]);
  Adder adder_1 (.a(A), .b(multiplexer_1_out), .out(adder_1_out), .cin(and_1_out));  // open: cout
  assign and_2_out = multiplexer_1_out & A;  // AND_Gate and_2, 8 bits wide
  assign or_1_out = multiplexer_1_out | A;  // OR_Gate or_1, 8 bits wide
  Multiplexer #(.select(2), .width(8), .enable("false")) multiplexer_2 (
    .in0(adder_1_out), .in1(and_2_out), .in2(or_1_out), .in3(adder_1_out), .out(ALU_Out), .sel(ALU_Op));

  // Notes on the sheet:
  //   8 bit ALU
  //   00 = ADD
  //   01 = AND
  //   10 = OR
  //   11 = SUB
  //   sub not B
  //   sub cin
  //   sub
endmodule

module RegisterFile (
  input  [7:0] Data_In,
  input  [2:0] Read_Addr_1,
  input  Write_Enable,
  input  [2:0] Write_Addr,
  input  [2:0] Read_Addr_2,
  input  Clock,
  output [7:0] Read_1_Data,
  output [7:0] Read_2_Data
);

  wire demultiplexer_1_out0, demultiplexer_1_out1, demultiplexer_1_out2, demultiplexer_1_out3,
       demultiplexer_1_out4, demultiplexer_1_out5, demultiplexer_1_out6, demultiplexer_1_out7;
  wire [7:0] register_1_q, register_2_q, register_3_q, register_4_q, register_5_q, register_6_q,
       register_7_q, register_8_q;

  Demultiplexer #(.select(3), .enable("false")) demultiplexer_1 (
    .out0(demultiplexer_1_out0), .out1(demultiplexer_1_out1), .out2(demultiplexer_1_out2),
    .out3(demultiplexer_1_out3), .out4(demultiplexer_1_out4), .out5(demultiplexer_1_out5),
    .out6(demultiplexer_1_out6), .out7(demultiplexer_1_out7), .in(Write_Enable), .sel(Write_Addr));
  Register register_1 (.D(Data_In), .en(demultiplexer_1_out0), .Q(register_1_q), .clk(Clock));  // open: clr
  Register register_2 (.D(Data_In), .en(demultiplexer_1_out1), .Q(register_2_q), .clk(Clock));  // open: clr
  Register register_3 (.D(Data_In), .en(demultiplexer_1_out2), .Q(register_3_q), .clk(Clock));  // open: clr
  Register register_4 (.D(Data_In), .en(demultiplexer_1_out3), .Q(register_4_q), .clk(Clock));  // open: clr
  Register register_5 (.D(Data_In), .en(demultiplexer_1_out4), .Q(register_5_q), .clk(Clock));  // open: clr
  Register register_6 (.D(Data_In), .en(demultiplexer_1_out5), .Q(register_6_q), .clk(Clock));  // open: clr
  Register register_7 (.D(Data_In), .en(demultiplexer_1_out6), .Q(register_7_q), .clk(Clock));  // open: clr
  Register register_8 (.D(Data_In), .en(demultiplexer_1_out7), .Q(register_8_q), .clk(Clock));  // open: clr
  Multiplexer #(.select(3), .width(8), .enable("false")) multiplexer_1 (
    .in0(register_1_q), .in1(register_2_q), .in2(register_3_q), .in3(register_4_q), .in4(register_5_q),
    .in5(register_6_q), .in6(register_7_q), .in7(register_8_q), .out(Read_1_Data), .sel(Read_Addr_1));
  Multiplexer #(.select(3), .width(8), .enable("false")) multiplexer_2 (
    .in0(register_1_q), .in1(register_2_q), .in2(register_3_q), .in3(register_4_q), .in4(register_5_q),
    .in5(register_6_q), .in6(register_7_q), .in7(register_8_q), .out(Read_2_Data), .sel(Read_Addr_2));

  // Notes on the sheet:
  //   8x4-bit Register File
endmodule

module _16X8Register (
  input  [7:0] Data_In,
  input  [3:0] ReadAddr1,
  input  Write_Enable,
  input  [3:0] Write_Addr,
  input  [3:0] ReadAddr2,
  input  Clock,
  output [7:0] Read_1_Data,
  output [7:0] Read_2_Data
);

  wire demultiplexer_1_out0, demultiplexer_1_out1, demultiplexer_1_out2, demultiplexer_1_out3,
       demultiplexer_1_out4, demultiplexer_1_out5, demultiplexer_1_out6, demultiplexer_1_out7,
       demultiplexer_1_out8, demultiplexer_1_out9, demultiplexer_1_out10, demultiplexer_1_out11,
       demultiplexer_1_out12, demultiplexer_1_out13, demultiplexer_1_out14, demultiplexer_1_out15;
  wire [7:0] register_1_q, register_2_q, register_3_q, register_4_q, register_5_q, register_6_q,
       register_7_q, register_8_q, register_9_q, register_10_q, register_11_q, register_12_q, register_13_q,
       register_14_q, register_15_q, register_16_q;

  Demultiplexer #(.select(4), .enable("false")) demultiplexer_1 (
    .out0(demultiplexer_1_out0), .out1(demultiplexer_1_out1), .out2(demultiplexer_1_out2),
    .out3(demultiplexer_1_out3), .out4(demultiplexer_1_out4), .out5(demultiplexer_1_out5),
    .out6(demultiplexer_1_out6), .out7(demultiplexer_1_out7), .out8(demultiplexer_1_out8),
    .out9(demultiplexer_1_out9), .out10(demultiplexer_1_out10), .out11(demultiplexer_1_out11),
    .out12(demultiplexer_1_out12), .out13(demultiplexer_1_out13), .out14(demultiplexer_1_out14),
    .out15(demultiplexer_1_out15), .in(Write_Enable), .sel(Write_Addr));
  Register register_1 (.D(Data_In), .en(demultiplexer_1_out0), .Q(register_1_q), .clk(Clock));  // open: clr
  Register register_2 (.D(Data_In), .en(demultiplexer_1_out1), .Q(register_2_q), .clk(Clock));  // open: clr
  Register register_3 (.D(Data_In), .en(demultiplexer_1_out2), .Q(register_3_q), .clk(Clock));  // open: clr
  Register register_4 (.D(Data_In), .en(demultiplexer_1_out3), .Q(register_4_q), .clk(Clock));  // open: clr
  Register register_5 (.D(Data_In), .en(demultiplexer_1_out4), .Q(register_5_q), .clk(Clock));  // open: clr
  Register register_6 (.D(Data_In), .en(demultiplexer_1_out5), .Q(register_6_q), .clk(Clock));  // open: clr
  Register register_7 (.D(Data_In), .en(demultiplexer_1_out6), .Q(register_7_q), .clk(Clock));  // open: clr
  Register register_8 (.D(Data_In), .en(demultiplexer_1_out7), .Q(register_8_q), .clk(Clock));  // open: clr
  Register register_9 (.D(Data_In), .en(demultiplexer_1_out8), .Q(register_9_q), .clk(Clock));  // open: clr
  Register register_10 (.D(Data_In), .en(demultiplexer_1_out9), .Q(register_10_q), .clk(Clock));  // open: clr
  Register register_11 (.D(Data_In), .en(demultiplexer_1_out10), .Q(register_11_q), .clk(Clock));  // open: clr
  Register register_12 (.D(Data_In), .en(demultiplexer_1_out11), .Q(register_12_q), .clk(Clock));  // open: clr
  Register register_13 (.D(Data_In), .en(demultiplexer_1_out12), .Q(register_13_q), .clk(Clock));  // open: clr
  Register register_14 (.D(Data_In), .en(demultiplexer_1_out13), .Q(register_14_q), .clk(Clock));  // open: clr
  Register register_15 (.D(Data_In), .en(demultiplexer_1_out14), .Q(register_15_q), .clk(Clock));  // open: clr
  Register register_16 (.D(Data_In), .en(demultiplexer_1_out15), .Q(register_16_q), .clk(Clock));  // open: clr
  Multiplexer #(.select(4), .width(8), .enable("false")) multiplexer_1 (
    .in0(register_1_q), .in1(register_2_q), .in2(register_3_q), .in3(register_4_q), .in4(register_5_q),
    .in5(register_6_q), .in6(register_7_q), .in7(register_8_q), .in8(register_9_q), .in9(register_10_q),
    .in10(register_11_q), .in11(register_12_q), .in12(register_13_q), .in13(register_14_q),
    .in14(register_15_q), .in15(register_16_q), .out(Read_1_Data), .sel(ReadAddr1));
  Multiplexer #(.select(4), .width(8), .enable("false")) multiplexer_2 (
    .in0(register_1_q), .in1(register_2_q), .in2(register_3_q), .in3(register_4_q), .in4(register_5_q),
    .in5(register_6_q), .in6(register_7_q), .in7(register_8_q), .in8(register_9_q), .in9(register_10_q),
    .in10(register_11_q), .in11(register_12_q), .in12(register_13_q), .in13(register_14_q),
    .in14(register_15_q), .in15(register_16_q), .out(Read_2_Data), .sel(ReadAddr2));

  // Notes on the sheet:
  //   16X8-bit Register File
endmodule

module R_and_I_instructions (
  input  sw,
  input  we,
  input  [7:0] DataIn,
  input  I,
  input  [1:0] OP,
  input  clk,
  input  [3:0] WriteAddr,
  input  [3:0] Source2,
  input  [3:0] Source1,
  output [7:0] ALU_out,
  output [7:0] RegisterValue2
);

  wire [3:0] multiplexer_1_out;
  wire [7:0] bit_extender_1_out, multiplexer_2_out, n16x8register_1_read_1_data;

  _16X8Register u_16x8register_1 (
    .Data_In(DataIn), .Write_Enable(we), .Clock(clk), .Write_Addr(WriteAddr), .ReadAddr1(Source1),
    .ReadAddr2(multiplexer_1_out), .Read_1_Data(n16x8register_1_read_1_data), .Read_2_Data(RegisterValue2));
  Multiplexer #(.width(4), .enable("false")) multiplexer_1 (
    .in0(Source2), .in1(WriteAddr), .out(multiplexer_1_out), .sel(sw));
  Multiplexer #(.width(8), .enable("false")) multiplexer_2 (
    .in0(RegisterValue2), .in1(bit_extender_1_out), .out(multiplexer_2_out), .sel(I));
  assign bit_extender_1_out = {{4{Source2[3]}}, Source2};  // Bit_Extender bit_extender_1
  ALU alu_1 (.A(n16x8register_1_read_1_data), .B(multiplexer_2_out), .ALU_Op(OP), .ALU_Out(ALU_out));
endmodule

module LW_and_SW (
  input  we,
  input  i,
  input  sw,
  input  lw,
  input  [1:0] ALU_OP,
  input  [3:0] Param1,
  input  [3:0] Param2,
  input  [3:0] Param3,
  input  clk,
  output [7:0] dataIn,
  output [7:0] ALU_out
);

  wire [7:0] ram_1_data, Register___ALU_registervalue2;

  R_and_I_instructions Register___ALU (
    .sw(sw), .we(we), .I(i), .OP(ALU_OP), .DataIn(dataIn), .WriteAddr(Param1), .Source1(Param2),
    .Source2(Param3), .clk(clk), .ALU_out(ALU_out), .RegisterValue2(Register___ALU_registervalue2));
  Multiplexer #(.width(8), .enable("false")) multiplexer_1 (.in0(ALU_out), .in1(ram_1_data), .out(dataIn), .sel(lw));
  RAM #(.bus("separate")) ram_1 (
    .addr(ALU_out), .din(Register___ALU_registervalue2), .data(ram_1_data), .str(sw), .sel(1'b1), .clk(clk),
    .ld(lw));  // open: clr

  // Notes on the sheet:
  //   SW?
  //   Lw?
  //   Data Memory
endmodule

module Control_Logic (
  input  [17:0] instructionWord,
  input  clk,
  output [7:0] Data_In,
  output [7:0] ALU_OUT,
  output [7:0] jump_inst,
  output j
);

  wire not_1_out;

  not not_1 (not_1_out, instructionWord[15]);
  LW_and_SW lw_and_sw_1 (
    .we(not_1_out), .i(instructionWord[16]), .sw(instructionWord[15]), .lw(instructionWord[14]),
    .ALU_OP(instructionWord[13:12]), .Param1(instructionWord[11:8]), .Param2(instructionWord[7:4]),
    .Param3(instructionWord[3:0]), .clk(clk), .dataIn(Data_In), .ALU_out(ALU_OUT));

  assign j = instructionWord[17];
  assign jump_inst = instructionWord[11:4];

  // Notes on the sheet:
  //   <J?><i?><sw?><lw?><op><par1><par2><par3>
endmodule

module InstructionMemory (
  input  enable,
  input  clk,
  output [7:0] data_in,
  output [7:0] alu_out,
  output [7:0] j_inst
);

  wire register_2_q, undriven;
  wire [7:0] adder_1_out, multiplexer_1_out, register_1_q;
  wire [17:0] ram_1_data;

  Adder adder_1 (.a(8'h1), .b(register_1_q), .out(adder_1_out));  // open: cin, cout
  Register register_1 (.D(adder_1_out), .en(enable), .Q(register_1_q), .clk(clk));  // open: clr
  Multiplexer #(.width(8), .enable("false")) multiplexer_1 (
    .in0(register_1_q), .in1(j_inst), .out(multiplexer_1_out), .sel(undriven));
  RAM #(.dataWidth(18)) ram_1 (.addr(multiplexer_1_out), .data(ram_1_data), .clk(clk));  // open: sel, ld, clr
  Register #(.width(1)) register_2 (.D(undriven), .Q(register_2_q), .clk(clk));  // open: en, clr
  Control_Logic control_logic_1 (
    .instructionWord(ram_1_data), .clk(clk), .Data_In(data_in), .ALU_OUT(alu_out), .jump_inst(j_inst),
    .j(register_2_q));
endmodule

module CPU___Test (
  input  enable,
  input  clk,
  output [7:0] Data_In,
  output [7:0] ALU_OUT,
  output [7:0] jump_inst
);

  wire not_1_out;
  wire [7:0] adder_1_out, multiplexer_1_out, register_1_q;
  wire [17:0] ram_1_data;

  Adder adder_1 (.a(8'h1), .b(register_1_q), .out(adder_1_out));  // open: cin, cout
  Register register_1 (.D(adder_1_out), .en(enable), .Q(register_1_q), .clk(clk));  // open: clr
  Multiplexer #(.width(8), .enable("false")) multiplexer_1 (
    .in0(register_1_q), .in1(jump_inst), .out(multiplexer_1_out), .sel(ram_1_data[17]));
  RAM #(.dataWidth(18)) ram_1 (
    .addr(multiplexer_1_out), .data({ram_1_data[17:12], jump_inst, ram_1_data[3:0]}), .clk(clk));  // open: sel, ld, clr
  not not_1 (not_1_out, ram_1_data[15]);
  LW_and_SW lw_and_sw_1 (
    .we(not_1_out), .i(ram_1_data[16]), .sw(ram_1_data[15]), .lw(ram_1_data[14]), .ALU_OP(ram_1_data[13:12]),
    .Param1(jump_inst[7:4]), .Param2(jump_inst[3:0]), .Param3(ram_1_data[3:0]), .clk(clk), .dataIn(Data_In),
    .ALU_out(ALU_OUT));
endmodule
