// Logisim project Shift.circ as structural Verilog
module ALU (
  input  [7:0] A,
  input  [7:0] B,
  input  [3:0] ALU_Op,
  output [7:0] ALU_Out
);

  wire and_1_out, comparator_1_eq, comparator_1_gt, comparator_1_lt, or_2_out;
  wire [2:0] bit_extender_1_out;
  wire [7:0] adder_1_out, and_2_out, bit_extender_2_out, bit_extender_3_out, bit_extender_4_out,
       multiplexer_1_out, not_1_out, not_2_out, or_1_out, shifter_1_out, shifter_2_out;

  Multiplexer #(.width(8), .enable("false")) multiplexer_1 (
    .in0(B), .in1(not_1_out), .out(multiplexer_1_out), .sel(and_1_out));
  assign not_1_out = ~B;  // NOT_Gate not_1, 8 bits wide
  Bit_Extender #(.out_width(3)) bit_extender_1 (.in(B), .out(bit_extender_1_out));
  and and_1 (and_1_out, ALU_Op[0], ALU_Op[1]);
  Adder adder_1 (.a(A), .b(multiplexer_1_out), .out(adder_1_out), .cin(and_1_out));  // open: cout
  assign and_2_out = multiplexer_1_out & A;  // AND_Gate and_2, 8 bits wide
  assign or_1_out = multiplexer_1_out | A;  // OR_Gate or_1, 8 bits wide
  Comparator comparator_1 (.a(A), .b(B), .gt(comparator_1_gt), .eq(comparator_1_eq), .lt(comparator_1_lt));
  assign bit_extender_2_out = {{7{comparator_1_eq}}, comparator_1_eq};  // Bit_Extender bit_extender_2
  assign bit_extender_3_out = {{7{comparator_1_lt}}, comparator_1_lt};  // Bit_Extender bit_extender_3
  or or_2 (or_2_out, comparator_1_eq, comparator_1_gt);
  Shifter shifter_1 (.in(A), .\dist (bit_extender_1_out), .out(shifter_1_out));
  Shifter #(.shift("lr")) shifter_2 (.in(A), .\dist (bit_extender_1_out), .out(shifter_2_out));
  assign not_2_out = ~bit_extender_2_out;  // NOT_Gate not_2, 8 bits wide
  assign bit_extender_4_out = {{7{or_2_out}}, or_2_out};  // Bit_Extender bit_extender_4
  Multiplexer #(.select(4), .width(8), .enable("false")) multiplexer_2 (
    .in0(adder_1_out), .in1(and_2_out), .in2(or_1_out), .in3(adder_1_out), .in4(bit_extender_2_out),
    .in5(not_2_out), .in6(bit_extender_3_out), .in7(bit_extender_4_out), .in8(shifter_1_out),
    .in9(shifter_2_out), .out(ALU_Out), .sel(ALU_Op));  // open: in10, in11, in12, in13, in14, in15

  // Notes on the sheet:
  //   8 bit ALU
  //   0000 = ADD
  //   0001 = AND
  //   sub not B
  //   0010 = OR
  //   sub cin
  //   0011 = SUB
  //   100 = eq
  //   sub
  //   0101 = neq
  //   0110 = blt
  //   0111 = beq
  //   1000 = sll
  //   1001 = slr
endmodule

module RegisterFile (
  input  [7:0] Data_In,
  input  [2:0] Read_Addr_1,
  input  Write_Enable,
  input  [2:0] Write_Addr,
  input  [2:0] Read_Addr_2,
  input  Clock,
  output [7:0] Read_1_Data,
  output [7:0] Read_2_Data
);

  wire demultiplexer_1_out0, demultiplexer_1_out1, demultiplexer_1_out2, demultiplexer_1_out3,
       demultiplexer_1_out4, demultiplexer_1_out5, demultiplexer_1_out6, demultiplexer_1_out7;
  wire [7:0] register_1_q, register_2_q, register_3_q, register_4_q, register_5_q, register_6_q,
       register_7_q, register_8_q;

  Demultiplexer #(.select(3), .enable("false")) demultiplexer_1 (
    .out0(demultiplexer_1_out0), .out1(demultiplexer_1_out1), .out2(demultiplexer_1_out2),
    .out3(demultiplexer_1_out3), .out4(demultiplexer_1_out4), .out5(demultiplexer_1_out5),
    .out6(demultiplexer_1_out6), .out7(demultiplexer_1_out7), .in(Write_Enable), .sel(Write_Addr));
  Register register_1 (.D(Data_In), .en(demultiplexer_1_out0), .Q(register_1_q), .clk(Clock));  // open: clr
  Register register_2 (.D(Data_In), .en(demultiplexer_1_out1), .Q(register_2_q), .clk(Clock));  // open: clr
  Register register_3 (.D(Data_In), .en(demultiplexer_1_out2), .Q(register_3_q), .clk(Clock));  // open: clr
  Register register_4 (.D(Data_In), .en(demultiplexer_1_out3), .Q(register_4_q), .clk(Clock));  // open: clr
  Register register_5 (.D(Data_In), .en(demultiplexer_1_out4), .Q(register_5_q), .clk(Clock));  // open: clr
  Register register_6 (.D(Data_In), .en(demultiplexer_1_out5), .Q(register_6_q), .clk(Clock));  // open: clr
  Register register_7 (.D(Data_In), .en(demultiplexer_1_out6), .Q(register_7_q), .clk(Clock));  // open: clr
  Register register_8 (.D(Data_In), .en(demultiplexer_1_out7), .Q(register_8_q), .clk(Clock));  // open: clr
  Multiplexer #(.select(3), .width(8), .enable("false")) multiplexer_1 (
    .in0(register_1_q), .in1(register_2_q), .in2(register_3_q), .in3(register_4_q), .in4(register_5_q),
    .in5(register_6_q), .in6(register_7_q), .in7(register_8_q), .out(Read_1_Data), .sel(Read_Addr_1));
  Multiplexer #(.select(3), .width(8), .enable("false")) multiplexer_2 (
    .in0(register_1_q), .in1(register_2_q), .in2(register_3_q), .in3(register_4_q), .in4(register_5_q),
    .in5(register_6_q), .in6(register_7_q), .in7(register_8_q), .out(Read_2_Data), .sel(Read_Addr_2));

  // Notes on the sheet:
  //   8x4-bit Register File
endmodule

module _16X8Register (
  input  [7:0] Data_In,
  input  [3:0] ReadAddr1,
  input  Write_Enable,
  input  [3:0] Write_Addr,
  input  [3:0] ReadAddr2,
  input  Clock,
  output [7:0] Read_1_Data,
  output [7:0] Read_2_Data
);

  wire demultiplexer_1_out0, demultiplexer_1_out1, demultiplexer_1_out2, demultiplexer_1_out3,
       demultiplexer_1_out4, demultiplexer_1_out5, demultiplexer_1_out6, demultiplexer_1_out7,
       demultiplexer_1_out8, demultiplexer_1_out9, demultiplexer_1_out10, demultiplexer_1_out11,
       demultiplexer_1_out12, demultiplexer_1_out13, demultiplexer_1_out14, demultiplexer_1_out15;
  wire [7:0] register_1_q, register_2_q, register_3_q, register_4_q, register_5_q, register_6_q,
       register_7_q, register_8_q, register_9_q, register_10_q, register_11_q, register_12_q, register_13_q,
       register_14_q, register_15_q, register_16_q;

  Demultiplexer #(.select(4), .enable("false")) demultiplexer_1 (
    .out0(demultiplexer_1_out0), .out1(demultiplexer_1_out1), .out2(demultiplexer_1_out2),
    .out3(demultiplexer_1_out3), .out4(demultiplexer_1_out4), .out5(demultiplexer_1_out5),
    .out6(demultiplexer_1_out6), .out7(demultiplexer_1_out7), .out8(demultiplexer_1_out8),
    .out9(demultiplexer_1_out9), .out10(demultiplexer_1_out10), .out11(demultiplexer_1_out11),
    .out12(demultiplexer_1_out12), .out13(demultiplexer_1_out13), .out14(demultiplexer_1_out14),
    .out15(demultiplexer_1_out15), .in(Write_Enable), .sel(Write_Addr));
  Register register_1 (.D(Data_In), .en(demultiplexer_1_out0), .Q(register_1_q), .clk(Clock));  // open: clr
  Register register_2 (.D(Data_In), .en(demultiplexer_1_out1), .Q(register_2_q), .clk(Clock));  // open: clr
  Register register_3 (.D(Data_In), .en(demultiplexer_1_out2), .Q(register_3_q), .clk(Clock));  // open: clr
  Register register_4 (.D(Data_In), .en(demultiplexer_1_out3), .Q(register_4_q), .clk(Clock));  // open: clr
  Register register_5 (.D(Data_In), .en(demultiplexer_1_out4), .Q(register_5_q), .clk(Clock));  // open: clr
  Register register_6 (.D(Data_In), .en(demultiplexer_1_out5), .Q(register_6_q), .clk(Clock));  // open: clr
  Register register_7 (.D(Data_In), .en(demultiplexer_1_out6), .Q(register_7_q), .clk(Clock));  // open: clr
  Register register_8 (.D(Data_In), .en(demultiplexer_1_out7), .Q(register_8_q), .clk(Clock));  // open: clr
  Register register_9 (.D(Data_In), .en(demultiplexer_1_out8), .Q(register_9_q), .clk(Clock));  // open: clr
  Register register_10 (.D(Data_In), .en(demultiplexer_1_out9), .Q(register_10_q), .clk(Clock));  // open: clr
  Register register_11 (.D(Data_In), .en(demultiplexer_1_out10), .Q(register_11_q), .clk(Clock));  // open: clr
  Register register_12 (.D(Data_In), .en(demultiplexer_1_out11), .Q(register_12_q), .clk(Clock));  // open: clr
  Register register_13 (.D(Data_In), .en(demultiplexer_1_out12), .Q(register_13_q), .clk(Clock));  // open: clr
  Register register_14 (.D(Data_In), .en(demultiplexer_1_out13), .Q(register_14_q), .clk(Clock));  // open: clr
  Register register_15 (.D(Data_In), .en(demultiplexer_1_out14), .Q(register_15_q), .clk(Clock));  // open: clr
  Register register_16 (.D(Data_In), .en(demultiplexer_1_out15), .Q(register_16_q), .clk(Clock));  // open: clr
  Multiplexer #(.select(4), .width(8), .enable("false")) multiplexer_1 (
    .in0(register_1_q), .in1(register_2_q), .in2(register_3_q), .in3(register_4_q), .in4(register_5_q),
    .in5(register_6_q), .in6(register_7_q), .in7(register_8_q), .in8(register_9_q), .in9(register_10_q),
    .in10(register_11_q), .in11(register_12_q), .in12(register_13_q), .in13(register_14_q),
    .in14(register_15_q), .in15(register_16_q), .out(Read_1_Data), .sel(ReadAddr1));
  Multiplexer #(.select(4), .width(8), .enable("false")) multiplexer_2 (
    .in0(register_1_q), .in1(register_2_q), .in2(register_3_q), .in3(register_4_q), .in4(register_5_q),
    .in5(register_6_q), .in6(register_7_q), .in7(register_8_q), .in8(register_9_q), .in9(register_10_q),
    .in10(register_11_q), .in11(register_12_q), .in12(register_13_q), .in13(register_14_q),
    .in14(register_15_q), .in15(register_16_q), .out(Read_2_Data), .sel(ReadAddr2));

  // Notes on the sheet:
  //   16X8-bit Register File
endmodule

module R_and_I_instructions (
  input  sw,
  input  we,
  input  [7:0] DataIn,
  input  I,
  input  [3:0] OP,
  input  clk,
  input  [3:0] Source2,
  input  [3:0] WriteAddr,
  input  [3:0] Source1,
  output [7:0] ALU_out,
  output [7:0] RegisterValue2
);

  wire comparator_1_eq, comparator_2_eq, or_1_out;
  wire [3:0] multiplexer_1_out;
  wire [7:0] bit_extender_1_out, bit_extender_2_out, multiplexer_2_out, multiplexer_3_out,
       n16x8register_1_read_1_data;

  _16X8Register u_16x8register_1 (
    .Data_In(DataIn), .Write_Enable(we), .Clock(clk), .Write_Addr(WriteAddr), .ReadAddr1(Source1),
    .ReadAddr2(multiplexer_1_out), .Read_1_Data(n16x8register_1_read_1_data), .Read_2_Data(RegisterValue2));
  Multiplexer #(.width(4), .enable("false")) multiplexer_1 (
    .in0(Source2), .in1(WriteAddr), .out(multiplexer_1_out), .sel(sw));
  Multiplexer #(.width(8), .enable("false")) multiplexer_2 (
    .in0(RegisterValue2), .in1(multiplexer_3_out), .out(multiplexer_2_out), .sel(I));
  assign bit_extender_1_out = {{4{1'b0}}, Source2};  // Bit_Extender bit_extender_1
  assign bit_extender_2_out = {{4{Source2[3]}}, Source2};  // Bit_Extender bit_extender_2
  ALU alu_1 (.A(n16x8register_1_read_1_data), .B(multiplexer_2_out), .ALU_Op(OP), .ALU_Out(ALU_out));
  Multiplexer #(.width(8), .enable("false")) multiplexer_3 (
    .in0(bit_extender_1_out), .in1(bit_extender_2_out), .out(multiplexer_3_out), .sel(or_1_out));
  Comparator #(.width(4)) comparator_1 (.a(4'b0000), .b(OP), .eq(comparator_1_eq));  // open: gt, lt
  or or_1 (or_1_out, comparator_1_eq, comparator_2_eq);
  Comparator #(.width(4)) comparator_2 (.a(4'b0011), .b(OP), .eq(comparator_2_eq));  // open: gt, lt

  // Notes on the sheet:
  //   Bit Extended immediate value
endmodule

module LW_and_SW (
  input  we,
  input  i,
  input  sw,
  input  lw,
  input  [3:0] ALU_OP,
  input  [3:0] Param1,
  input  [3:0] Param2,
  input  [3:0] Param3,
  input  clk,
  output [7:0] dataIn,
  output [7:0] ALU_out
);

  wire [7:0] ram_1_data, Register___ALU_registervalue2;

  R_and_I_instructions Register___ALU (
    .sw(sw), .we(we), .I(i), .OP(ALU_OP), .DataIn(dataIn), .WriteAddr(Param1), .Source1(Param2),
    .Source2(Param3), .clk(clk), .ALU_out(ALU_out), .RegisterValue2(Register___ALU_registervalue2));
  Multiplexer #(.width(8), .enable("false")) multiplexer_1 (.in0(ALU_out), .in1(ram_1_data), .out(dataIn), .sel(lw));
  RAM #(.bus("separate")) ram_1 (
    .addr(ALU_out), .din(Register___ALU_registervalue2), .data(ram_1_data), .str(sw), .sel(1'b1), .clk(clk),
    .ld(lw));  // open: clr

  // Notes on the sheet:
  //   SW?
  //   Lw?
  //   Data Memory
endmodule

module Control_Logic (
  input  [19:0] instructionWord,
  input  clk,
  output [7:0] Data_In,
  output [7:0] ALU_OUt,
  output [7:0] J_Inst,
  output [7:0] Branch_OFF,
  output J,
  output B
);

  wire not_1_out, not_2_out, or_1_out;

  or or_1 (or_1_out, instructionWord[19], instructionWord[17]);
  not not_1 (not_1_out, or_1_out);
  LW_and_SW lw_and_sw_1 (
    .we(not_1_out), .i(instructionWord[18]), .sw(instructionWord[17]), .lw(instructionWord[16]),
    .ALU_OP(instructionWord[15:12]), .Param1(instructionWord[11:8]), .Param2(instructionWord[7:4]),
    .Param3(instructionWord[3:0]), .clk(clk), .dataIn(Data_In), .ALU_out(ALU_OUt));
  assign Branch_OFF = {{4{instructionWord[11]}}, instructionWord[11:8]};  // Bit_Extender bit_extender_1
  Multiplexer #(.width(8), .enable("false")) multiplexer_1 (
    .in0(instructionWord[11:4]), .in1(ALU_OUt), .out(J_Inst), .sel(instructionWord[18]));
  not not_2 (not_2_out, instructionWord[14]);
  and and_1 (J, not_2_out, instructionWord[19]);
  and and_2 (B, instructionWord[14], ALU_OUt[7], instructionWord[19]);

  // Notes on the sheet:
  //   <J?><i?><sw?><lw?><op><par1><par2><par3>
  //   j?
  //   sw?
  //   op code
  //   j?
  //   we?
  //   Branch if J?, the first alu is 1, and if the alu output is 1
endmodule

module InstructionMemory (
  input  enable,
  input  clk,
  output [7:0] data_in,
  output [7:0] alu_out,
  output [7:0] j_inst,
  output [7:0] Branch_Off
);

  wire control_logic_1_b, control_logic_1_j;
  wire [7:0] adder_1_out, multiplexer_1_out, multiplexer_2_out, register_1_q;
  wire [19:0] ram_1_data;

  Multiplexer #(.width(8), .enable("false")) multiplexer_1 (
    .in0(8'h1), .in1(Branch_Off), .out(multiplexer_1_out), .sel(control_logic_1_b));
  Adder adder_1 (.a(multiplexer_1_out), .b(register_1_q), .out(adder_1_out));  // open: cin, cout
  Register register_1 (.D(multiplexer_2_out), .en(enable), .Q(register_1_q), .clk(clk));  // open: clr
  Multiplexer #(.width(8), .enable("false")) multiplexer_2 (
    .in0(adder_1_out), .in1(j_inst), .out(multiplexer_2_out), .sel(control_logic_1_j));
  RAM #(.dataWidth(20)) ram_1 (.addr(register_1_q), .data(ram_1_data), .clk(clk));  // open: sel, ld, clr
  Control_Logic control_logic_1 (
    .instructionWord(ram_1_data), .clk(clk), .Data_In(data_in), .ALU_OUt(alu_out), .J_Inst(j_inst),
    .Branch_OFF(Branch_Off), .J(control_logic_1_j), .B(control_logic_1_b));

  // Notes on the sheet:
  //   b?
  //   branch Off
  //   j inst
  //   j?
endmodule

module CPU___Test (
  input  [18:0] instructionWord,
  input  clk,
  output [7:0] Data_In,
  output [7:0] ALU_OUt,
  output [7:0] J_Inst,
  output [7:0] Branch_OFF,
  output J,
  output B
);

  wire not_1_out, not_2_out, or_1_out;
  wire [3:3] undriven;

  or or_1 (or_1_out, instructionWord[18], instructionWord[16]);
  not not_1 (not_1_out, or_1_out);
  LW_and_SW lw_and_sw_1 (
    .we(not_1_out), .i(instructionWord[17]), .sw(instructionWord[16]), .lw(instructionWord[15]),
    .ALU_OP({undriven[3], instructionWord[14:12]}), .Param1(instructionWord[11:8]),
    .Param2(instructionWord[7:4]), .Param3(instructionWord[3:0]), .clk(clk), .dataIn(Data_In),
    .ALU_out(ALU_OUt));
  assign Branch_OFF = {{4{instructionWord[11]}}, instructionWord[11:8]};  // Bit_Extender bit_extender_1
  Multiplexer #(.width(8), .enable("false")) multiplexer_1 (
    .in0(instructionWord[11:4]), .in1(ALU_OUt), .out(J_Inst), .sel(instructionWord[17]));
  not not_2 (not_2_out, instructionWord[14]);
  and and_1 (J, not_2_out, instructionWord[18]);
  and and_2 (B, instructionWord[14], ALU_OUt[7], instructionWord[18]);
  // Pins of 3 and 4 bits meet at {undriven[3], instructionWord[14:12]}

  // Notes on the sheet:
  //   <J?><i?><sw?><lw?><op><par1><par2><par3>
  //   j?
  //   sw?
  //   op code
  //   j?
  //   we?
  //   Dest
  //   ALU OUT
  //   imm?
  //   Branch if J?, the first alu is 1, and if the alu output is 1
endmodule
